// Logisim project l64.circ as structural Verilog: 12 circuits, main circuit main
module main (
);

  wire and_1_out, clock_1_out, comparator_1_eq, MemEnable, MemWrite, Reset_out;
  wire [1:0] Size;
  wire [7:0] rom_1_p2, rom_1_p3, rom_1_p4, rom_1_p5, rom_1_p6, rom_1_p7, rom_1_p8, rom_1_p9;
  wire [63:0] Address, cpu_1_writedata, Data, memorytruncater_1_data;

  // ROM #(.addrWidth(16), .line("octo"), .misaligned("true")) rom_1: pin names not known; wires that end beside it: Address[15:0], rom_1_p2, rom_1_p3, rom_1_p4, rom_1_p5, rom_1_p6, rom_1_p7, rom_1_p8, rom_1_p9
  Clock clock_1 (.out(clock_1_out));
  Button Reset (.out(Reset_out));
  CPU cpu_1 (
    .ReadData(Data), .Clock(clock_1_out), .Reset(Reset_out), .MemoryEnable(MemEnable),
    .WriteEnable(MemWrite), .WriteData(cpu_1_writedata), .Address(Address), .Size(Size));
  assign Data = MemWrite ? cpu_1_writedata : 64'bz;  // Controlled_Buffer controlled_buffer_1
  MemoryTruncater memorytruncater_1 (
    .Size(Size), .Byte0(rom_1_p2), .Byte1(rom_1_p3), .Byte2(rom_1_p4), .Byte3(rom_1_p5), .Byte4(rom_1_p6),
    .Byte5(rom_1_p7), .Byte6(rom_1_p8), .Byte7(rom_1_p9), .Data(memorytruncater_1_data));
  Comparator #(.mode("unsigned"), .width(48)) comparator_1 (
    .a(Address[63:16]), .b({48{1'b0}}), .eq(comparator_1_eq));  // open: gt, lt
  and and_1 (and_1_out, comparator_1_eq, MemEnable, ~MemWrite);  // AND_Gate
  assign Data = and_1_out ? memorytruncater_1_data : 64'bz;  // Controlled_Buffer controlled_buffer_2
endmodule

module RegFile4 (
  input  Write0Enable,
  input  Write1Enable,
  input  [1:0] Write0Reg,
  input  [1:0] Write1Reg,
  input  [63:0] Write0Data,
  input  [63:0] Write1Data,
  input  [1:0] Read0Reg,
  input  [1:0] Read1Reg,
  input  [1:0] Read2Reg,
  input  Clock,
  input  Reset,
  output [63:0] Read0Out,
  output [63:0] Read1Out,
  output [63:0] Read2Out
);

  wire demultiplexer_1_out0, demultiplexer_1_out1, demultiplexer_1_out2, demultiplexer_1_out3,
       demultiplexer_2_out0, demultiplexer_2_out1, demultiplexer_2_out2, demultiplexer_2_out3, or_1_out,
       or_2_out, or_3_out, or_4_out;
  wire [63:0] multiplexer_1_out, multiplexer_2_out, multiplexer_3_out, multiplexer_4_out, register_1_q,
       register_2_q, register_3_q, register_4_q;

  Demultiplexer #(.select(2)) demultiplexer_1 (
    .out0(demultiplexer_1_out0), .out1(demultiplexer_1_out1), .out2(demultiplexer_1_out2),
    .out3(demultiplexer_1_out3), .in(Write0Enable), .sel(Write0Reg));
  Demultiplexer #(.select(2)) demultiplexer_2 (
    .out0(demultiplexer_2_out0), .out1(demultiplexer_2_out1), .out2(demultiplexer_2_out2),
    .out3(demultiplexer_2_out3), .in(Write1Enable), .sel(Write1Reg));
  Multiplexer #(.width(64)) multiplexer_1 (
    .in0(Write0Data), .in1(Write1Data), .out(multiplexer_1_out), .sel(demultiplexer_2_out0));
  or or_1 (or_1_out, demultiplexer_2_out0, demultiplexer_1_out0);
  Multiplexer #(.width(64)) multiplexer_2 (
    .in0(Write0Data), .in1(Write1Data), .out(multiplexer_2_out), .sel(demultiplexer_2_out1));
  or or_2 (or_2_out, demultiplexer_2_out1, demultiplexer_1_out1);
  Multiplexer #(.width(64)) multiplexer_3 (
    .in0(Write0Data), .in1(Write1Data), .out(multiplexer_3_out), .sel(demultiplexer_2_out2));
  or or_3 (or_3_out, demultiplexer_2_out2, demultiplexer_1_out2);
  Multiplexer #(.width(64)) multiplexer_4 (
    .in0(Write0Data), .in1(Write1Data), .out(multiplexer_4_out), .sel(demultiplexer_2_out3));
  or or_4 (or_4_out, demultiplexer_2_out3, demultiplexer_1_out3);
  Register #(.width(64)) register_1 (.D(multiplexer_1_out), .en(or_1_out), .clk(Clock), .Q(register_1_q), .clr(Reset));
  Register #(.width(64)) register_2 (.D(multiplexer_2_out), .en(or_2_out), .clk(Clock), .Q(register_2_q), .clr(Reset));
  Register #(.width(64)) register_3 (.D(multiplexer_3_out), .en(or_3_out), .clk(Clock), .Q(register_3_q), .clr(Reset));
  Register #(.width(64)) register_4 (.D(multiplexer_4_out), .en(or_4_out), .clk(Clock), .Q(register_4_q), .clr(Reset));
  Multiplexer #(.select(2), .width(64)) multiplexer_5 (
    .in0(register_1_q), .in1(register_2_q), .in2(register_3_q), .in3(register_4_q), .out(Read0Out),
    .sel(Read0Reg));
  Multiplexer #(.select(2), .width(64)) multiplexer_6 (
    .in0(register_1_q), .in1(register_2_q), .in2(register_3_q), .in3(register_4_q), .out(Read1Out),
    .sel(Read1Reg));
  Multiplexer #(.select(2), .width(64)) multiplexer_7 (
    .in0(register_1_q), .in1(register_2_q), .in2(register_3_q), .in3(register_4_q), .out(Read2Out),
    .sel(Read2Reg));
endmodule

module RegFile16 (
  input  Write0Enable,
  input  Write1Enable,
  input  [3:0] Write0Reg,
  input  [3:0] Write1Reg,
  input  [63:0] Write0Data,
  input  [63:0] Write1Data,
  input  [3:0] Read0Reg,
  input  [3:0] Read1Reg,
  input  [3:0] Read2Reg,
  input  Reset,
  input  Clock,
  output [63:0] Read0Out,
  output [63:0] Read1Out,
  output [63:0] Read2Out
);

  wire demultiplexer_1_out0, demultiplexer_1_out1, demultiplexer_1_out2, demultiplexer_1_out3,
       demultiplexer_2_out0, demultiplexer_2_out1, demultiplexer_2_out2, demultiplexer_2_out3;
  wire [63:0] regfile4_1_read0out, regfile4_1_read1out, regfile4_1_read2out, regfile4_2_read0out,
       regfile4_2_read1out, regfile4_2_read2out, regfile4_3_read0out, regfile4_3_read1out,
       regfile4_3_read2out, regfile4_4_read0out, regfile4_4_read1out, regfile4_4_read2out;

  Demultiplexer #(.select(2)) demultiplexer_1 (
    .out0(demultiplexer_1_out0), .out1(demultiplexer_1_out1), .out2(demultiplexer_1_out2),
    .out3(demultiplexer_1_out3), .in(Write1Enable), .sel(Write1Reg[3:2]));
  Demultiplexer #(.select(2)) demultiplexer_2 (
    .out0(demultiplexer_2_out0), .out1(demultiplexer_2_out1), .out2(demultiplexer_2_out2),
    .out3(demultiplexer_2_out3), .in(Write0Enable), .sel(Write0Reg[3:2]));
  RegFile4 regfile4_1 (
    .Write0Enable(demultiplexer_2_out0), .Write1Enable(demultiplexer_1_out0), .Write0Reg(Write0Reg[1:0]),
    .Write1Reg(Write1Reg[1:0]), .Write0Data(Write0Data), .Write1Data(Write1Data), .Read0Reg(Read0Reg[1:0]),
    .Read1Reg(Read1Reg[1:0]), .Read2Reg(Read2Reg[1:0]), .Clock(Clock), .Reset(Reset),
    .Read0Out(regfile4_1_read0out), .Read1Out(regfile4_1_read1out), .Read2Out(regfile4_1_read2out));
  RegFile4 regfile4_2 (
    .Write0Enable(demultiplexer_2_out1), .Write1Enable(demultiplexer_1_out1), .Write0Reg(Write0Reg[1:0]),
    .Write1Reg(Write1Reg[1:0]), .Write0Data(Write0Data), .Write1Data(Write1Data), .Read0Reg(Read0Reg[1:0]),
    .Read1Reg(Read1Reg[1:0]), .Read2Reg(Read2Reg[1:0]), .Clock(Clock), .Reset(Reset),
    .Read0Out(regfile4_2_read0out), .Read1Out(regfile4_2_read1out), .Read2Out(regfile4_2_read2out));
  RegFile4 regfile4_3 (
    .Write0Enable(demultiplexer_2_out2), .Write1Enable(demultiplexer_1_out2), .Write0Reg(Write0Reg[1:0]),
    .Write1Reg(Write1Reg[1:0]), .Write0Data(Write0Data), .Write1Data(Write1Data), .Read0Reg(Read0Reg[1:0]),
    .Read1Reg(Read1Reg[1:0]), .Read2Reg(Read2Reg[1:0]), .Clock(Clock), .Reset(Reset),
    .Read0Out(regfile4_3_read0out), .Read1Out(regfile4_3_read1out), .Read2Out(regfile4_3_read2out));
  RegFile4 regfile4_4 (
    .Write0Enable(demultiplexer_2_out3), .Write1Enable(demultiplexer_1_out3), .Write0Reg(Write0Reg[1:0]),
    .Write1Reg(Write1Reg[1:0]), .Write0Data(Write0Data), .Write1Data(Write1Data), .Read0Reg(Read0Reg[1:0]),
    .Read1Reg(Read1Reg[1:0]), .Read2Reg(Read2Reg[1:0]), .Clock(Clock), .Reset(Reset),
    .Read0Out(regfile4_4_read0out), .Read1Out(regfile4_4_read1out), .Read2Out(regfile4_4_read2out));
  Multiplexer #(.select(2), .width(64)) multiplexer_1 (
    .in0(regfile4_1_read0out), .in1(regfile4_2_read0out), .in2(regfile4_3_read0out),
    .in3(regfile4_4_read0out), .out(Read0Out), .sel(Read0Reg[3:2]));
  Multiplexer #(.select(2), .width(64)) multiplexer_2 (
    .in0(regfile4_1_read1out), .in1(regfile4_2_read1out), .in2(regfile4_3_read1out),
    .in3(regfile4_4_read1out), .out(Read1Out), .sel(Read1Reg[3:2]));
  Multiplexer #(.select(2), .width(64)) multiplexer_3 (
    .in0(regfile4_1_read2out), .in1(regfile4_2_read2out), .in2(regfile4_3_read2out),
    .in3(regfile4_4_read2out), .out(Read2Out), .sel(Read2Reg[3:2]));
endmodule

module RegFile (
  input  Write0Enable,
  input  Write1Enable,
  input  [3:0] Write0Reg,
  input  [3:0] Write1Reg,
  input  [63:0] Write0Data,
  input  [63:0] Write1Data,
  input  [3:0] Read0Reg,
  input  [3:0] Read1Reg,
  input  [3:0] Read2Reg,
  input  Reset,
  input  Clock,
  output [63:0] Read0Out,
  output [63:0] Read1Out,
  output [63:0] Read2Out
);

  wire comparator_1_eq, comparator_2_eq, comparator_3_eq;
  wire [63:0] regfile16_1_read0out, regfile16_1_read1out, regfile16_1_read2out;

  Comparator #(.mode("unsigned"), .width(4)) comparator_1 (
    .a(Read0Reg), .b(4'b0000), .eq(comparator_1_eq));  // open: gt, lt
  Comparator #(.mode("unsigned"), .width(4)) comparator_2 (
    .a(Read1Reg), .b(4'b0000), .eq(comparator_2_eq));  // open: gt, lt
  Comparator #(.mode("unsigned"), .width(4)) comparator_3 (
    .a(Read2Reg), .b(4'b0000), .eq(comparator_3_eq));  // open: gt, lt
  RegFile16 regfile16_1 (
    .Write0Enable(Write0Enable), .Write1Enable(Write1Enable), .Write0Reg(Write0Reg), .Write1Reg(Write1Reg),
    .Write0Data(Write0Data), .Write1Data(Write1Data), .Read0Reg(Read0Reg), .Read1Reg(Read1Reg),
    .Read2Reg(Read2Reg), .Reset(Reset), .Clock(Clock), .Read0Out(regfile16_1_read0out),
    .Read1Out(regfile16_1_read1out), .Read2Out(regfile16_1_read2out));
  Multiplexer #(.disabled("Z"), .width(64)) multiplexer_1 (
    .in0(regfile16_1_read0out), .in1({64{1'b0}}), .out(Read0Out), .sel(comparator_1_eq));
  Multiplexer #(.disabled("Z"), .width(64)) multiplexer_2 (
    .in0(regfile16_1_read1out), .in1({64{1'b0}}), .out(Read1Out), .sel(comparator_2_eq));
  Multiplexer #(.disabled("Z"), .width(64)) multiplexer_3 (
    .in0(regfile16_1_read2out), .in1({64{1'b0}}), .out(Read2Out), .sel(comparator_3_eq));
endmodule

module ALU (
  input  [5:0] Op,
  input  [63:0] A,
  input  [63:0] B,
  input  [63:0] C,
  output [63:0] O,
  output [63:0] I
);

  wire adder_1_cout, bit_extender_9_out, comparator_1_eq, decoder_1_out0, decoder_1_out1, decoder_1_out2,
       decoder_1_out3, decoder_1_out4, decoder_1_out5, decoder_1_out6, decoder_1_out7, decoder_1_out8,
       decoder_1_out9, decoder_1_out10, decoder_1_out16, decoder_1_out17, not_1_out, not_2_out,
       subtractor_1_bout;
  wire [4:0] decoder_1_out11;
  wire [5:0] bit_extender_3_out, bit_extender_12_out, bit_extender_13_out;
  wire [7:0] bit_extender_8_out;
  wire [15:0] bit_extender_5_out;
  wire [31:0] bit_extender_4_out;
  wire [63:0] adder_1_out, adder_2_out, adder_3_out, adder_4_out, adder_5_out, adder_6_out, and_1_out,
       bit_extender_1_out, bit_extender_2_out, bit_extender_6_out, bit_extender_7_out, bit_extender_10_out,
       bit_extender_11_out, multiplier_1_cout, multiplier_1_out, multiplier_2_cout, multiplier_2_out,
       negator_1_out, or_1_out, or_2_out, or_3_out, or_4_out, shifter_1_out, shifter_2_out, shifter_3_out,
       shifter_4_out, subtractor_1_out, xor_1_out;

  not not_1 (not_1_out, Op[0]);
  not not_2 (not_2_out, comparator_1_eq);
  Comparator #(.mode("unsigned"), .width(64)) comparator_1 (
    .a(C), .b({64{1'b0}}), .eq(comparator_1_eq));  // open: gt, lt
  assign and_1_out = C & B & A;  // AND_Gate and_1, 64 bits wide
  assign O = decoder_1_out0 ? and_1_out : 64'bz;  // Controlled_Buffer controlled_buffer_1
  assign or_1_out = C | B | A;  // OR_Gate or_1, 64 bits wide
  assign I = decoder_1_out0 ? or_1_out : 64'bz;  // Controlled_Buffer controlled_buffer_2
  assign O = decoder_1_out1 ? ~A : 64'bz;  // Controlled_Inverter controlled_inverter_1
  Negator #(.width(64)) negator_1 (.in(A), .out(negator_1_out));
  assign I = decoder_1_out1 ? negator_1_out : 64'bz;  // Controlled_Buffer controlled_buffer_3
  assign xor_1_out = B ^ A;  // XOR_Gate xor_1, 64 bits wide
  assign I = decoder_1_out2 ? xor_1_out : 64'bz;  // Controlled_Buffer controlled_buffer_4
  Multiplexer #(.disabled("Z"), .enable("true"), .width(64)) multiplexer_1 (
    .in0(B), .in1(A), .out(O), .sel(not_2_out), .en(decoder_1_out2));
  Adder #(.width(64)) adder_1 (.a(A), .b(B), .out(adder_1_out), .cin(not_2_out), .cout(adder_1_cout));
  assign bit_extender_1_out = {{63{1'b0}}, adder_1_cout};  // Bit_Extender bit_extender_1
  assign I = decoder_1_out3 ? bit_extender_1_out : 64'bz;  // Controlled_Buffer controlled_buffer_5
  assign O = decoder_1_out3 ? adder_1_out : 64'bz;  // Controlled_Buffer controlled_buffer_6
  Subtractor #(.width(64)) subtractor_1 (
    .a(A), .b(B), .out(subtractor_1_out), .bin(not_2_out), .bout(subtractor_1_bout));
  assign bit_extender_2_out = {{63{1'b0}}, subtractor_1_bout};  // Bit_Extender bit_extender_2
  assign I = decoder_1_out4 ? bit_extender_2_out : 64'bz;  // Controlled_Buffer controlled_buffer_7
  assign O = decoder_1_out4 ? subtractor_1_out : 64'bz;  // Controlled_Buffer controlled_buffer_8
  assign I = decoder_1_out5 ? multiplier_1_cout : 64'bz;  // Controlled_Buffer controlled_buffer_9
  Multiplier #(.width(64)) multiplier_1 (.a(A), .b(B), .out(multiplier_1_out), .cin(C), .cout(multiplier_1_cout));
  assign O = decoder_1_out5 ? multiplier_1_out : 64'bz;  // Controlled_Buffer controlled_buffer_10
  Multiplier #(.mode("twosComplement"), .width(64)) multiplier_2 (
    .a(A), .b(B), .out(multiplier_2_out), .cin(C), .cout(multiplier_2_cout));
  assign I = decoder_1_out6 ? multiplier_2_cout : 64'bz;  // Controlled_Buffer controlled_buffer_11
  assign O = decoder_1_out6 ? multiplier_2_out : 64'bz;  // Controlled_Buffer controlled_buffer_12
  Bit_Extender #(.in_width(64), .out_width(6), .\type ("zero")) bit_extender_3 (.in(B), .out(bit_extender_3_out));
  Shifter #(.width(64)) shifter_1 (.in(A), .\dist (bit_extender_3_out), .out(shifter_1_out));
  Adder #(.width(64)) adder_2 (.a(shifter_1_out), .b(C), .out(adder_2_out), .cin(1'b0));  // open: cout
  assign O = decoder_1_out7 ? adder_2_out : 64'bz;  // Controlled_Buffer controlled_buffer_13
  Decoder #(.select(5)) decoder_1 (
    .out0(decoder_1_out0), .out1(decoder_1_out1), .out2(decoder_1_out2), .out3(decoder_1_out3),
    .out4(decoder_1_out4), .out5(decoder_1_out5), .out6(decoder_1_out6), .out7(decoder_1_out7),
    .out8(decoder_1_out8), .out9(decoder_1_out9), .out10(decoder_1_out10), .out11(decoder_1_out11[0]),
    .out12(decoder_1_out11[1]), .out13(decoder_1_out11[2]), .out14(decoder_1_out11[3]),
    .out15(decoder_1_out11[4]), .out16(decoder_1_out16), .out17(decoder_1_out17), .sel(Op[5:1]),
    .en(not_1_out));  // open: out18, out19, out20, out21, out22, out23, out24, out25, out26, out27, out28, out29, out30, out31
  Shifter #(.width(64)) shifter_2 (.in(A), .\dist (6'b110010), .out(shifter_2_out));
  assign I = decoder_1_out7 ? adder_3_out : 64'bz;  // Controlled_Buffer controlled_buffer_14
  assign or_2_out = shifter_2_out | B;  // OR_Gate or_2, 64 bits wide
  Adder #(.width(64)) adder_3 (.a(C), .b(or_2_out), .out(adder_3_out), .cin(1'b0));  // open: cout
  Bit_Extender #(.in_width(64), .out_width(32), .\type ("zero")) bit_extender_4 (.in(A), .out(bit_extender_4_out));
  Bit_Extender #(.in_width(64), .\type ("zero")) bit_extender_5 (.in(A), .out(bit_extender_5_out));
  assign bit_extender_6_out = {{32{bit_extender_4_out[31]}}, bit_extender_4_out};  // Bit_Extender bit_extender_6
  assign bit_extender_7_out = {{48{bit_extender_5_out[15]}}, bit_extender_5_out};  // Bit_Extender bit_extender_7
  assign I = decoder_1_out8 ? bit_extender_7_out : 64'bz;  // Controlled_Buffer controlled_buffer_15
  assign O = decoder_1_out8 ? bit_extender_6_out : 64'bz;  // Controlled_Buffer controlled_buffer_16
  Bit_Extender #(.in_width(64), .out_width(8), .\type ("zero")) bit_extender_8 (.in(A), .out(bit_extender_8_out));
  Bit_Extender #(.in_width(64), .out_width(1), .\type ("zero")) bit_extender_9 (.in(A), .out(bit_extender_9_out));
  assign bit_extender_10_out = {{56{bit_extender_8_out[7]}}, bit_extender_8_out};  // Bit_Extender bit_extender_10
  assign bit_extender_11_out = {{63{bit_extender_9_out}}, bit_extender_9_out};  // Bit_Extender bit_extender_11
  assign I = decoder_1_out9 ? bit_extender_11_out : 64'bz;  // Controlled_Buffer controlled_buffer_17
  assign O = decoder_1_out9 ? bit_extender_10_out : 64'bz;  // Controlled_Buffer controlled_buffer_18
  Bit_Extender #(.in_width(64), .out_width(6), .\type ("zero")) bit_extender_12 (.in(B), .out(bit_extender_12_out));
  Shifter #(.shift("lr"), .width(64)) shifter_3 (.in(A), .\dist (bit_extender_12_out), .out(shifter_3_out));
  Adder #(.width(64)) adder_4 (.a(shifter_3_out), .b(C), .out(adder_4_out), .cin(1'b0));  // open: cout
  assign O = decoder_1_out10 ? adder_4_out : 64'bz;  // Controlled_Buffer controlled_buffer_19
  assign I = decoder_1_out10 ? adder_5_out : 64'bz;  // Controlled_Buffer controlled_buffer_20
  Bit_Extender #(.in_width(64), .out_width(6), .\type ("zero")) bit_extender_13 (.in(B), .out(bit_extender_13_out));
  Shifter #(.shift("ar"), .width(64)) shifter_4 (.in(A), .\dist (bit_extender_13_out), .out(shifter_4_out));
  Adder #(.width(64)) adder_5 (.a(shifter_4_out), .b(C), .out(adder_5_out), .cin(1'b0));  // open: cout
  ComparatorUnit comparatorunit_1 (.Op(decoder_1_out11), .A(A), .B(B), .O(O), .I(I));
  assign or_3_out = A | C;  // OR_Gate or_3, 64 bits wide
  assign or_4_out = B | C;  // OR_Gate or_4, 64 bits wide
  assign O = decoder_1_out16 ? or_3_out : 64'bz;  // Controlled_Buffer controlled_buffer_21
  assign I = decoder_1_out16 ? or_4_out : 64'bz;  // Controlled_Buffer controlled_buffer_22
  Adder #(.width(64)) adder_6 (.a(A), .b(B), .out(adder_6_out), .cin(1'b0));  // open: cout
  assign O = decoder_1_out17 ? adder_6_out : 64'bz;  // Controlled_Buffer controlled_buffer_23
  assign I = decoder_1_out17 ? C : 64'bz;  // Controlled_Buffer controlled_buffer_24
endmodule

module CPU (
  input  [63:0] ReadData,
  input  Clock,
  input  Reset,
  output MemoryEnable,
  output WriteEnable,
  output [63:0] WriteData,
  output [63:0] Address,
  output [1:0] Size
);

  wire aludriver_1_writeflags, ConnectAddress, ConnectMemory, microcode_1_addressmode,
       microcode_1_cycledisable, microcode_1_flagsmode, microcode_1_memoryenable, microcode_1_memorywrite,
       microcode_1_pretendloadstate, microcode_1_regwrite0enable, microcode_1_regwrite1enable,
       microcode_1_statereset, not_1_out, or_1_out, State_qn, StateExecute, StateLoad;
  wire [1:0] addressunit_1_size, instructiondecoder_1_loadsize, instructiondecoder_1_storesize,
       microcode_1_immediatemode;
  wire [3:0] Cycle_q, multiplexer_1_out, multiplexer_2_out;
  wire [4:0] Opcode;
  wire [5:0] ALUOp;
  wire [11:0] instructiondecoder_1_loadscale, instructiondecoder_1_storescale;
  wire [19:0] Registers;
  wire [63:0] adder_1_out, addressunit_1_address, alu_1_i, alu_1_o, aludriver_1_a, aludriver_1_b,
       aludriver_1_c, Flags_q, Immediate, InstructionLatch_q, multiplexer_3_out, multiplexer_4_out,
       multiplexer_5_out, Src0, Src1;

  Multiplexer #(.disabled("Z"), .width(4)) multiplexer_1 (
    .in0(Registers[3:0]), .in1(4'b1111), .out(multiplexer_1_out), .sel(StateLoad));
  Multiplexer #(.disabled("Z"), .width(4)) multiplexer_2 (
    .in0(Registers[11:8]), .in1(4'b1111), .out(multiplexer_2_out), .sel(StateLoad));
  or or_1 (or_1_out, StateLoad, microcode_1_regwrite0enable);
  Microcode microcode_1 (
    .Opcode(Opcode), .Cycle(Cycle_q), .Enable(StateExecute), .RegWrite0Enable(microcode_1_regwrite0enable),
    .RegWrite1Enable(microcode_1_regwrite1enable), .ImmediateMode(microcode_1_immediatemode),
    .FlagsMode(microcode_1_flagsmode), .MemoryEnable(microcode_1_memoryenable),
    .MemoryWrite(microcode_1_memorywrite), .CycleDisable(microcode_1_cycledisable),
    .StateReset(microcode_1_statereset), .AddressMode(microcode_1_addressmode),
    .ConnectMemory(ConnectMemory), .ConnectAddress(ConnectAddress),
    .PretendLoadState(microcode_1_pretendloadstate));
  RegFile regfile_1 (
    .Write0Enable(or_1_out), .Write1Enable(microcode_1_regwrite1enable), .Write0Reg(multiplexer_1_out),
    .Write1Reg(Registers[7:4]), .Write0Data(multiplexer_3_out), .Write1Data(alu_1_i),
    .Read0Reg(multiplexer_2_out), .Read1Reg(Registers[15:12]), .Read2Reg(Registers[19:16]), .Reset(Reset),
    .Clock(Clock), .Read0Out(Src0), .Read1Out(Src1), .Read2Out(WriteData));
  Counter #(.max('hf), .width(4)) Cycle (
    .clr(1'b0), .load(StateLoad), .up(1'b1), .count(not_1_out), .clk(Clock), .D(4'b0000), .Q(Cycle_q));  // open: carry
  not not_1 (not_1_out, microcode_1_cycledisable);
  S_R_Flip_Flop State (
    .S(StateLoad), .R(microcode_1_statereset), .clk(Clock), .Q(StateExecute), .reset(Reset), .Qn(State_qn));  // open: preset
  Multiplexer #(.disabled("Z"), .width(64)) multiplexer_3 (
    .in0(multiplexer_4_out), .in1(adder_1_out), .out(multiplexer_3_out), .sel(StateLoad));
  Adder #(.width(64)) adder_1 (.a(64'h8), .b(Src0), .out(adder_1_out), .cin(1'b0));  // open: cout
  or or_2 (StateLoad, State_qn, microcode_1_pretendloadstate);
  Register #(.width(64)) InstructionLatch (
    .D(ReadData), .en(StateLoad), .clk(Clock), .Q(InstructionLatch_q), .clr(Reset));
  InstructionDecoder instructiondecoder_1 (
    .Instruction(InstructionLatch_q), .OpCode(Opcode), .ALUOp(ALUOp), .Immediate(Immediate),
    .Src0(Registers[11:8]), .Src1(Registers[15:12]), .Dst0(Registers[3:0]), .Src2(Registers[19:16]),
    .Dst1(Registers[7:4]), .StoreScale(instructiondecoder_1_storescale),
    .LoadScale(instructiondecoder_1_loadscale), .StoreSize(instructiondecoder_1_storesize),
    .LoadSize(instructiondecoder_1_loadsize));
  ALUDriver aludriver_1 (
    .Reg0(Src0), .Reg1(Src1), .Reg2(WriteData), .Immediate(Immediate), .Flags(Flags_q),
    .ImmediateMode(microcode_1_immediatemode), .FlagsMode(microcode_1_flagsmode), .A(aludriver_1_a),
    .B(aludriver_1_b), .C(aludriver_1_c), .WriteFlags(aludriver_1_writeflags));
  Register #(.width(64)) Flags (.D(alu_1_i), .en(aludriver_1_writeflags), .clk(Clock), .Q(Flags_q), .clr(Reset));
  ALU alu_1 (.Op(ALUOp), .A(aludriver_1_a), .B(aludriver_1_b), .C(aludriver_1_c), .O(alu_1_o), .I(alu_1_i));
  Multiplexer #(.disabled("Z"), .width(64)) multiplexer_4 (
    .in0(alu_1_o), .in1(multiplexer_5_out), .out(multiplexer_4_out), .sel(ConnectAddress));
  Multiplexer #(.disabled("Z"), .width(64)) multiplexer_5 (
    .in0(Address), .in1(ReadData), .out(multiplexer_5_out), .sel(ConnectMemory));
  Multiplexer #(.width(64)) multiplexer_6 (.in0(addressunit_1_address), .in1(Src0), .out(Address), .sel(StateLoad));
  AddressUnit addressunit_1 (
    .Base(Src0), .Offset(Immediate), .Index(Src1), .StoreScale(instructiondecoder_1_storescale),
    .LoadScale(instructiondecoder_1_loadscale), .StoreSize(instructiondecoder_1_storesize),
    .LoadSize(instructiondecoder_1_loadsize), .Mode(microcode_1_addressmode),
    .Address(addressunit_1_address), .Size(addressunit_1_size));
  or or_3 (MemoryEnable, microcode_1_memoryenable, StateLoad);
  and and_1 (WriteEnable, microcode_1_memorywrite, ~StateLoad);  // AND_Gate
  Multiplexer #(.width(2)) multiplexer_7 (.in0(addressunit_1_size), .in1(2'b11), .out(Size), .sel(StateLoad));

  // Other names for the same wires on the sheet: Src2[63:0] = WriteData
endmodule

module ALUDriver (
  input  [63:0] Reg0,
  input  [63:0] Reg1,
  input  [63:0] Reg2,
  input  [63:0] Immediate,
  input  [63:0] Flags,
  input  [1:0] ImmediateMode,
  input  FlagsMode,
  output [63:0] A,
  output [63:0] B,
  output [63:0] C,
  output WriteFlags
);

  wire decoder_1_out1, decoder_1_out2, decoder_1_out3;
  wire [63:0] multiplexer_1_out;

  Decoder #(.enable("false"), .select(2)) decoder_1 (
    .out1(decoder_1_out1), .out2(decoder_1_out2), .out3(decoder_1_out3), .sel(ImmediateMode));  // open: out0
  Multiplexer #(.width(64)) multiplexer_1 (.in0(Reg2), .in1(Immediate), .out(multiplexer_1_out), .sel(decoder_1_out3));
  Multiplexer #(.width(64)) multiplexer_2 (.in0(Reg0), .in1(Immediate), .out(A), .sel(decoder_1_out1));
  Multiplexer #(.width(64)) multiplexer_3 (.in0(Reg1), .in1(Immediate), .out(B), .sel(decoder_1_out2));
  Multiplexer #(.width(64)) multiplexer_4 (.in0(multiplexer_1_out), .in1(Flags), .out(C), .sel(FlagsMode));

  assign WriteFlags = FlagsMode;
endmodule

module InstructionDecoder (
  input  [63:0] Instruction,
  output [4:0] OpCode,
  output [5:0] ALUOp,
  output [63:0] Immediate,
  output [3:0] Src0,
  output [3:0] Src1,
  output [3:0] Dst0,
  output [3:0] Src2,
  output [3:0] Dst1,
  output [11:0] StoreScale,
  output [11:0] LoadScale,
  output [1:0] StoreSize,
  output [1:0] LoadSize
);

  assign Immediate = {{31{Instruction[63]}}, Instruction[63:31]};  // Bit_Extender bit_extender_1

  assign ALUOp = Instruction[30:25];
  assign Dst0 = Instruction[16:13];
  assign Dst1 = Instruction[24:21];
  assign LoadScale = Instruction[30:19];
  assign LoadSize = Instruction[18:17];
  assign OpCode = Instruction[4:0];
  assign Src0 = Instruction[8:5];
  assign Src1 = Instruction[12:9];
  assign Src2 = Instruction[20:17];
  assign StoreScale = {Instruction[30:21], Instruction[16:15]};
  assign StoreSize = Instruction[14:13];
endmodule

module ComparatorUnit (
  input  [4:0] Op,
  input  [63:0] A,
  input  [63:0] B,
  output [63:0] O,
  output [63:0] I
);

  wire comparator_1_eq, comparator_1_gt, comparator_1_lt, comparator_2_gt, comparator_2_lt,
       controlled_buffer_1_out, controlled_inverter_1_out, or_1_out;
  wire [63:0] bit_extender_1_out, bit_extender_2_out;

  Comparator #(.width(64)) comparator_1 (
    .a(A), .b(B), .gt(comparator_1_gt), .eq(comparator_1_eq), .lt(comparator_1_lt));
  Comparator #(.mode("unsigned"), .width(64)) comparator_2 (
    .a(A), .b(A), .gt(comparator_2_gt), .lt(comparator_2_lt));  // open: eq
  assign controlled_inverter_1_out = Op[4] ? ~comparator_2_gt : 1'bz;  // Controlled_Inverter controlled_inverter_1
  assign controlled_inverter_1_out = Op[3] ? ~comparator_2_lt : 1'bz;  // Controlled_Inverter controlled_inverter_2
  assign controlled_inverter_1_out = Op[2] ? ~comparator_1_gt : 1'bz;  // Controlled_Inverter controlled_inverter_3
  assign controlled_inverter_1_out = Op[1] ? ~comparator_1_lt : 1'bz;  // Controlled_Inverter controlled_inverter_4
  assign controlled_inverter_1_out = Op[0] ? ~comparator_1_eq : 1'bz;  // Controlled_Inverter controlled_inverter_5
  or or_1 (or_1_out, Op[0], Op[1], Op[2], Op[3], Op[4]);
  assign controlled_buffer_1_out = Op[4] ? comparator_2_gt : 1'bz;  // Controlled_Buffer controlled_buffer_1
  assign controlled_buffer_1_out = Op[3] ? comparator_2_lt : 1'bz;  // Controlled_Buffer controlled_buffer_2
  assign controlled_buffer_1_out = Op[2] ? comparator_1_gt : 1'bz;  // Controlled_Buffer controlled_buffer_3
  assign controlled_buffer_1_out = Op[1] ? comparator_1_lt : 1'bz;  // Controlled_Buffer controlled_buffer_4
  assign controlled_buffer_1_out = Op[0] ? comparator_1_eq : 1'bz;  // Controlled_Buffer controlled_buffer_5
  assign bit_extender_1_out = {{63{1'b0}}, controlled_buffer_1_out};  // Bit_Extender bit_extender_1
  assign bit_extender_2_out = {{63{1'b0}}, controlled_inverter_1_out};  // Bit_Extender bit_extender_2
  assign I = or_1_out ? bit_extender_2_out : 64'bz;  // Controlled_Buffer controlled_buffer_6
  assign O = or_1_out ? bit_extender_1_out : 64'bz;  // Controlled_Buffer controlled_buffer_7
endmodule

module AddressUnit (
  input  [63:0] Base,
  input  [63:0] Offset,
  input  [63:0] Index,
  input  [11:0] StoreScale,
  input  [11:0] LoadScale,
  input  [1:0] StoreSize,
  input  [1:0] LoadSize,
  input  Mode,
  output [63:0] Address,
  output [1:0] Size
);

  wire [11:0] multiplexer_1_out;
  wire [63:0] adder_1_out, adder_2_out, bit_extender_1_out, multiplier_1_out;

  Adder #(.width(64)) adder_1 (.a(Base), .b(Offset), .out(adder_1_out), .cin(1'b0));  // open: cout
  assign bit_extender_1_out = {{52{1'b0}}, multiplexer_1_out};  // Bit_Extender bit_extender_1
  Multiplexer #(.width(12)) multiplexer_1 (.in0(StoreScale), .in1(LoadScale), .out(multiplexer_1_out), .sel(Mode));
  Multiplexer #(.width(2)) multiplexer_2 (.in0(StoreSize), .in1(LoadSize), .out(Size), .sel(Mode));
  Multiplier #(.width(64)) multiplier_1 (
    .a(Index), .b(adder_2_out), .out(multiplier_1_out), .cin({64{1'b0}}));  // open: cout
  Adder #(.width(64)) adder_2 (.a(bit_extender_1_out), .b({64{1'b0}}), .out(adder_2_out), .cin(1'b1));  // open: cout
  Adder #(.width(64)) adder_3 (.a(adder_1_out), .b(multiplier_1_out), .out(Address), .cin(1'b0));  // open: cout
endmodule

module Microcode (
  input  [4:0] Opcode,
  input  [3:0] Cycle,
  input  Enable,
  output RegWrite0Enable,
  output RegWrite1Enable,
  output [1:0] ImmediateMode,
  output FlagsMode,
  output MemoryEnable,
  output MemoryWrite,
  output CycleDisable,
  output StateReset,
  output AddressMode,
  output ConnectMemory,
  output ConnectAddress,
  output PretendLoadState
);

  wire [12:0] pla_1_out;

  PLA #(.in_width(9), .out_width(13), .\table ("000000000 1000000000000 # NOP Cycle 0")) pla_1 (
    .in({Opcode, Cycle}), .out(pla_1_out));
  and and_1 (RegWrite0Enable, pla_1_out[0], Enable);
  and and_2 (RegWrite1Enable, pla_1_out[1], Enable);
  Multiplexer #(.disabled("Z"), .width(2)) multiplexer_1 (
    .in0(2'b00), .in1(pla_1_out[3:2]), .out(ImmediateMode), .sel(Enable));
  and and_3 (FlagsMode, pla_1_out[4], Enable);
  and and_4 (MemoryEnable, pla_1_out[5], Enable);
  and and_5 (MemoryWrite, pla_1_out[6], Enable);
  and and_6 (CycleDisable, pla_1_out[7], Enable);
  and and_7 (StateReset, pla_1_out[8], Enable);
  and and_8 (AddressMode, pla_1_out[9], Enable);
  and and_9 (ConnectMemory, pla_1_out[10], Enable);
  and and_10 (ConnectAddress, pla_1_out[11], Enable);
  and and_11 (PretendLoadState, pla_1_out[12], Enable);
endmodule

module MemoryTruncater (
  input  [1:0] Size,
  input  [7:0] Byte0,
  input  [7:0] Byte1,
  input  [7:0] Byte2,
  input  [7:0] Byte3,
  input  [7:0] Byte4,
  input  [7:0] Byte5,
  input  [7:0] Byte6,
  input  [7:0] Byte7,
  output [63:0] Data
);

  wire and_1_out, or_1_out;

  Multiplexer #(.disabled("Z"), .width(8)) multiplexer_1 (
    .in0({8{1'b0}}), .in1(Byte1), .out(Data[15:8]), .sel(or_1_out));
  Multiplexer #(.disabled("Z"), .width(16)) multiplexer_2 (
    .in0({16{1'b0}}), .in1({Byte3, Byte2}), .out(Data[31:16]), .sel(Size[1]));
  Multiplexer #(.disabled("Z"), .width(32)) multiplexer_3 (
    .in0({32{1'b0}}), .in1({Byte7, Byte6, Byte5, Byte4}), .out(Data[63:32]), .sel(and_1_out));
  or or_1 (or_1_out, Size[0], Size[1]);
  and and_1 (and_1_out, Size[0], Size[1]);

  assign Data[7:0] = Byte0;
endmodule
